# Fritzing sketch pawsfzz (saved by Fritzing 0.9.6b)
breadboards: 1

parts:
  uPesy_ESP32_Wrover_DevKit1 = uPesy ESP32 Wrover DevKit v2
  Composant1 = Barometric Pressure Sensor - BMP180 Breakout (GY-68)  # not connected
  ZS-042_RTC1 = ZS-042 RTC Module  # not connected
  S1 = Pushbutton [package="[THT]"]
  R1 = Resistor [tolerance=±5% power=0.25 resistance=220 package=THT]
  microSD1 = MicroSD Card Module  # not connected

nets:
  N1: uPesy_ESP32_Wrover_DevKit1.3V3, R1.Pin_1
  N2: S1.Pin_1, S1.Pin_2, R1.Pin_0
  N3: S1.Pin_3, S1.Pin_4

custom parts:
  uPesy ESP32 Wrover DevKit v2: ESP32 development board that is 100% breadboard compatible with 4MB PSRAM and USB-C connector
